# Fritzing sketch ravenhid (saved by Fritzing 0.8.3b)
circuit board: 6cm x 4cm
breadboards: 1

parts:
  Vcc_Ctr_Pos = Power plug
  +5Vreg = Voltage Regulator - 5V [package="TO220 [THT]"]
  Reset = Pushbutton [package="[THT]"]
  1MΩ = Resistor [tolerance=±5% resistance=1M package=THT]
  +5V_GND_Vcc = male pin header, 3 pins [form="♂ (male)"]
  Diode = Rectifier Diode [part_number=1N4004 package="300 mil [THT]"]
  0_1µF = Ceramic Capacitor [capacitance=0.1µF voltage=50V package="100 mil [THT, multilayer]"]
  100pF = Ceramic Capacitor [capacitance=100pF voltage=50V package="100 mil [THT, multilayer]"]
  0_1µF_2 = Ceramic Capacitor [capacitance=0.1µF voltage=50V package="100 mil [THT, multilayer]"]
  10kΩ = Resistor [tolerance=±5% resistance=10k package=THT]
  10µF = Ceramic Capacitor [capacitance=10µF package="100 mil [THT, multilayer]"]
  FTDI = male pin header, 6 pins [form="♂ (male)"]
  47µF = Electrolytic Capacitor [capacitance=47µF voltage=50V package="100 mil [THT, electrolytic]"]
  16MHz = Resonator [frequency="16 Mhz" package=THT]
  BLEMini = female pin header, 4 pins [form="♀ (female)"]
  MicroSD = MicroSD Breakout
  R1 = Resistor [tolerance=±5% resistance=10k package=THT]
  Arduino_Uno_(ATMega328) = atmega168 [package="DIP28 [THT]"]
  LCD = Adafruit Negative RGB 2x16 LCD
  Contrast = TRIMPOT [package=trim_pot_pth]
  RFID = screw terminal, 4 pins

nets:
  GND: Vcc_Ctr_Pos.GND, +5Vreg.GND, Reset.Pin_3, Reset.Pin_4, +5V_GND_Vcc.pin2, 0_1µF.0, 100pF.0, 10µF.1, FTDI.pin1, 47µF.-, 16MHz.GND, BLEMini.pin2, MicroSD.GND, Arduino_Uno_(ATMega328).Pin_8, Arduino_Uno_(ATMega328).Pin_22, LCD.no_name_yet#0, LCD.no_name_yet#4, Contrast.CCW, RFID.pin1
  N1: Vcc_Ctr_Pos.VCC, Diode.anode
  12V: +5Vreg.input_voltage, +5V_GND_Vcc.pin3, Diode.cathode, 0_1µF.1, 100pF.1, 47µF.+, RFID.pin4
  5V: +5Vreg.output_voltage, +5V_GND_Vcc.pin1, 10kΩ.Pin_0, 10µF.0, FTDI.pin3, BLEMini.pin1, MicroSD.5V, R1.Pin_1, Arduino_Uno_(ATMega328).Pin_7, Arduino_Uno_(ATMega328).Pin_20, LCD.no_name_yet#1, LCD.no_name_yet#14, Contrast.CW
  N2: Reset.Pin_1, Reset.Pin_2, 0_1µF_2.1, Arduino_Uno_(ATMega328).Pin_1
  N3: 1MΩ.Pin_0, 16MHz.0, Arduino_Uno_(ATMega328).Pin_9
  N4: 1MΩ.Pin_1, 16MHz.pin_1, Arduino_Uno_(ATMega328).Pin_10
  N5: 0_1µF_2.0, 10kΩ.Pin_1, FTDI.pin6
  N6: FTDI.pin4, BLEMini.pin3, Arduino_Uno_(ATMega328).Pin_2
  N7: FTDI.pin5, BLEMini.pin4, Arduino_Uno_(ATMega328).Pin_3
  N8: MicroSD.CD, R1.Pin_0, Arduino_Uno_(ATMega328).Pin_15
  N9: MicroSD.CS, Arduino_Uno_(ATMega328).Pin_16
  N10: MicroSD.DI, Arduino_Uno_(ATMega328).Pin_17
  N11: MicroSD.DO, Arduino_Uno_(ATMega328).Pin_18
  N12: MicroSD.CLK, Arduino_Uno_(ATMega328).Pin_19
  N13: Arduino_Uno_(ATMega328).Pin_4, RFID.pin2
  N14: Arduino_Uno_(ATMega328).Pin_5, RFID.pin3
  N15: Arduino_Uno_(ATMega328).Pin_11, LCD.no_name_yet#13
  N16: Arduino_Uno_(ATMega328).Pin_12, LCD.no_name_yet#12
  N17: Arduino_Uno_(ATMega328).Pin_13, LCD.no_name_yet#11
  N18: Arduino_Uno_(ATMega328).Pin_14, LCD.no_name_yet#10
  N19: Arduino_Uno_(ATMega328).Pin_23, LCD.no_name_yet#3
  N20: Arduino_Uno_(ATMega328).Pin_24, LCD.no_name_yet#5
  N21: Arduino_Uno_(ATMega328).Pin_25, LCD.no_name_yet#15
  N22: Arduino_Uno_(ATMega328).Pin_26, LCD.no_name_yet#16
  N23: Arduino_Uno_(ATMega328).Pin_27, LCD.no_name_yet#17
  N24: LCD.no_name_yet#2, Contrast.WIPER

notes:
  RavenHID
  D7
  VIN
  GND
  TX
  RX
  D0
  D1
  12v
  https://github.com/emperorcow/ravenhid
  Designed By:
  Lucas Morris
  Adam Zamora
  v1.1
  CTS
  5V
  RTS
  RFID

custom parts:
  MicroSD Breakout: 5V-ready microSD Breakout with Level Shifter
  Adafruit Negative RGB 2x16 LCD: Adafruit Negative 2x16 LCD Display with RGB Backlight
